# Fritzing sketch Akıllı Baret Devre Şeması (saved by Fritzing 0.9.4)
breadboards: 1

parts:
  U1 = NodeMCU V1.0
  M1 = DHT11-Grove-Temperature-Sensor_1
  IC1 = MQ-2 [package="DIP (Dual Inline) [THT]"]
  Parça1 = InvenSense MPU6050
  HC-SR04_Sensor_1 = HC-SR04 Ultrasonic Distance Sensor
  J1 = Piezo Speaker
  R1 = Resistor [tolerance=±5% resistance=220 package="1206 [SMD]"]
  S1 = Pushbutton [package="[SMD]"]
  R2 = Resistor [tolerance=±5% resistance=220 package="2010 [SMD]"]

nets:
  N1: U1.D0, M1.connector0
  N2: U1.D1, U1.D5, U1.D6, U1.D7, U1.D8, U1.GND#13, M1.connector3, IC1.pin2, Parça1.SCL, HC-SR04_Sensor_1.TRIG, HC-SR04_Sensor_1.ECHO, HC-SR04_Sensor_1.GND, S1.Pin_1, S1.Pin_2, R2.Pin_0
  N3: U1.D2, Parça1.SDA
  N4: U1.D4, J1.pin2
  N5: U1.Vin, M1.connector2, IC1.pin1
  N6: U1.GND#16, R1.Pin_0, R2.Pin_1
  N7: U1.A0, IC1.pin4
  N8: J1.pin1, R1.Pin_1
  N9: S1.Pin_3, S1.Pin_4

custom parts:
  NodeMCU V1.0: ESP8266 based NodeMCU V1.0
  MQ-2: MQ-2 Gas Sensor module
